# Fritzing sketch ESP32-Soil-Sentinel (saved by Fritzing 0.9.6b)
breadboards: 1

parts:
  Capacitive_Soil_Moisture_Sensor1 = DFRobot Capacitive Soil Moisture Sensor V1.0 [part_number=SEN0193]
  Componente1 = LCD1602-I2C
  S2 = Pushbutton [package="[THT]"]
  S3 = Pushbutton [package="[THT]"]
  S4 = Pushbutton [package="[THT]"]
  CPU1 = NodeMCU WROOM ESP 32
  A1 = DHT22 module

nets:
  N1: Capacitive_Soil_Moisture_Sensor1.A, CPU1.pin_17, A1.+, A1.-
  N2: Capacitive_Soil_Moisture_Sensor1.VCC, CPU1.pin_5
  N3: Capacitive_Soil_Moisture_Sensor1.GND, S2.Pin_1, S2.Pin_2, S3.Pin_1, S3.Pin_2, S4.Pin_1, S4.Pin_2, CPU1.pin_18
  N4: Componente1.GND, CPU1.pin_15
  N5: Componente1.VCC, CPU1.pin_16
  N6: Componente1.SDA, CPU1.pin_27
  N7: Componente1.SCL, CPU1.pin_30
  N8: S2.Pin_3, S2.Pin_4, CPU1.pin_13
  N9: S3.Pin_3, S3.Pin_4, CPU1.pin_12
  N10: S4.Pin_3, S4.Pin_4, CPU1.pin_14
  N11: CPU1.pin_6, A1.Out

custom parts:
  DFRobot Capacitive Soil Moisture Sensor V1.0: DFRobot Capacitive Soil Moisture Sensor V1.0 This product measures soil moisture levels by capacitive sensing, rather than resistive sensing like other types of moisture sensor. It is made of a corrosion resistant material giving it a long service life. Insert it into soil and impress your friends with the real-time soil moisture data! The product includes an on-board voltage regulator which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
  LCD1602-I2C: A standard character display, usually with 2x16 characters. Comes in many colors with LCM1602 IIC attached.
  NodeMCU WROOM ESP 32: 30 pol Development Kit
  DHT22 module: DHT22 module. Pins VCC Data GND.
